// Logisim project 4-1mux_1.circ as structural Verilog: 1 circuit, main circuit main
module main (
  input  s1,
  input  s0,
  input  x0,
  input  x1,
  input  x2,
  input  x3,
  output y
);

  wire and_1_out, and_2_out, and_3_out, and_4_out, not_1_out, not_2_out;

  not not_1 (not_1_out, s1);
  not not_2 (not_2_out, s0);
  and and_1 (and_1_out, x0, not_1_out, not_2_out);
  and and_2 (and_2_out, x1, not_1_out, s0);
  and and_3 (and_3_out, x2, s1, not_2_out);
  and and_4 (and_4_out, x3, s1, s0);
  or or_1 (y, and_1_out, and_2_out, and_3_out, and_4_out);

  // Notes on the sheet:
  //   4 to 1 Multiplexer
endmodule
