// Logisim project 8bitnot_1.circ as structural Verilog: 1 circuit, main circuit main
module main (
  input  in_1,
  input  a0,
  input  a0_2,
  input  a1,
  input  a1_2,
  input  a2,
  input  a2_2,
  input  a3,
  input  a3_2,
  input  a4,
  input  a4_2,
  input  a5,
  input  a5_2,
  input  a6,
  input  a6_2,
  input  a7,
  input  a7_2,
  output c0,
  output c0_2,
  output c1,
  output c1_2,
  output c2,
  output c2_2,
  output c3,
  output c3_2,
  output c4,
  output c4_2,
  output c5,
  output c5_2,
  output c6,
  output c6_2,
  output c7,
  output c7_2
);

  wire not_1_out, not_2_out, not_3_out, not_4_out, not_5_out, not_6_out, not_7_out, not_8_out;

  not not_1 (not_1_out, a0);
  not not_2 (not_2_out, a1);
  not not_3 (not_3_out, a2);
  not not_4 (not_4_out, a3);
  not not_5 (not_5_out, a4);
  not not_6 (not_6_out, a5);
  not not_7 (not_7_out, a6);
  not not_8 (not_8_out, a7);
  assign c0 = in_1 ? not_1_out : 1'bz;  // Controlled_Buffer controlled_buffer_1
  assign c1 = in_1 ? not_2_out : 1'bz;  // Controlled_Buffer controlled_buffer_2
  assign c2 = in_1 ? not_3_out : 1'bz;  // Controlled_Buffer controlled_buffer_3
  assign c3 = in_1 ? not_4_out : 1'bz;  // Controlled_Buffer controlled_buffer_4
  assign c4 = in_1 ? not_5_out : 1'bz;  // Controlled_Buffer controlled_buffer_5
  assign c5 = in_1 ? not_6_out : 1'bz;  // Controlled_Buffer controlled_buffer_6
  assign c6 = in_1 ? not_7_out : 1'bz;  // Controlled_Buffer controlled_buffer_7
  assign c7 = in_1 ? not_8_out : 1'bz;  // Controlled_Buffer controlled_buffer_8
  not not_9 (c0_2, a0_2);
  not not_10 (c1_2, a1_2);
  not not_11 (c2_2, a2_2);
  not not_12 (c3_2, a3_2);
  not not_13 (c4_2, a4_2);
  not not_14 (c5_2, a5_2);
  not not_15 (c6_2, a6_2);
  not not_16 (c7_2, a7_2);

  // Notes on the sheet:
  //   8 Bit Not Logic
endmodule
