// Logisim project 8bitor_1.circ as structural Verilog: 1 circuit, main circuit main
module main (
  input  in_1,
  input  a0,
  input  a0_2,
  input  b0,
  input  b0_2,
  input  a1,
  input  a1_2,
  input  b1,
  input  b1_2,
  input  a2,
  input  a2_2,
  input  b2,
  input  b2_2,
  input  a3,
  input  a3_2,
  input  b3,
  input  b3_2,
  input  a4,
  input  a4_2,
  input  b4,
  input  b4_2,
  input  a5,
  input  a5_2,
  input  b5,
  input  b5_2,
  input  a6,
  input  a6_2,
  input  b6,
  input  b6_2,
  input  a7,
  input  a7_2,
  input  b7,
  input  b7_2,
  output c0,
  output c0_2,
  output c1,
  output c1_2,
  output c2,
  output c2_2,
  output c3,
  output c3_2,
  output c4,
  output c4_2,
  output c5,
  output c5_2,
  output c6,
  output c6_2,
  output c7,
  output c7_2
);

  wire or_1_out, or_2_out, or_3_out, or_4_out, or_5_out, or_6_out, or_7_out, or_8_out;

  or or_1 (or_1_out, a0, b0);
  or or_2 (or_2_out, a1, b1);
  or or_3 (or_3_out, a2, b2);
  or or_4 (or_4_out, a3, b3);
  or or_5 (or_5_out, a4, b4);
  or or_6 (or_6_out, a5, b5);
  or or_7 (or_7_out, a6, b6);
  or or_8 (or_8_out, a7, b7);
  assign c0 = in_1 ? or_1_out : 1'bz;  // Controlled_Buffer controlled_buffer_1
  assign c1 = in_1 ? or_2_out : 1'bz;  // Controlled_Buffer controlled_buffer_2
  assign c2 = in_1 ? or_3_out : 1'bz;  // Controlled_Buffer controlled_buffer_3
  assign c3 = in_1 ? or_4_out : 1'bz;  // Controlled_Buffer controlled_buffer_4
  assign c4 = in_1 ? or_5_out : 1'bz;  // Controlled_Buffer controlled_buffer_5
  assign c5 = in_1 ? or_6_out : 1'bz;  // Controlled_Buffer controlled_buffer_6
  assign c6 = in_1 ? or_7_out : 1'bz;  // Controlled_Buffer controlled_buffer_7
  assign c7 = in_1 ? or_8_out : 1'bz;  // Controlled_Buffer controlled_buffer_8
  or or_9 (c0_2, a0_2, b0_2);
  or or_10 (c1_2, a1_2, b1_2);
  or or_11 (c2_2, a2_2, b2_2);
  or or_12 (c3_2, a3_2, b3_2);
  or or_13 (c4_2, a4_2, b4_2);
  or or_14 (c5_2, a5_2, b5_2);
  or or_15 (c6_2, a6_2, b6_2);
  or or_16 (c7_2, a7_2, b7_2);

  // Notes on the sheet:
  //   8-Bit Or Logic
endmodule
