// Logisim project 8bitxor_1.circ as structural Verilog: 1 circuit, main circuit main
module main (
  input  in_1,
  input  a0,
  input  a0_2,
  input  b0,
  input  b0_2,
  input  a1,
  input  a1_2,
  input  b1,
  input  b1_2,
  input  a2,
  input  a2_2,
  input  b2,
  input  b2_2,
  input  a3,
  input  a3_2,
  input  b3,
  input  b3_2,
  input  a4,
  input  a4_2,
  input  b4,
  input  b4_2,
  input  a5,
  input  a5_2,
  input  b5,
  input  b5_2,
  input  a6,
  input  a6_2,
  input  b6,
  input  b6_2,
  input  a7,
  input  a7_2,
  input  b7,
  input  b7_2,
  output c0,
  output c0_2,
  output c1,
  output c1_2,
  output c2,
  output c2_2,
  output c3,
  output c3_2,
  output c4,
  output c4_2,
  output c5,
  output c5_2,
  output c6,
  output c6_2,
  output c7,
  output c7_2
);

  wire xor_1_out, xor_2_out, xor_3_out, xor_4_out, xor_5_out, xor_6_out, xor_7_out, xor_8_out;

  xor xor_1 (xor_1_out, a0, b0);
  xor xor_2 (xor_2_out, a1, b1);
  xor xor_3 (xor_3_out, a2, b2);
  xor xor_4 (xor_4_out, a3, b3);
  xor xor_5 (xor_5_out, a4, b4);
  xor xor_6 (xor_6_out, a5, b5);
  xor xor_7 (xor_7_out, a6, b6);
  xor xor_8 (xor_8_out, a7, b7);
  assign c0 = in_1 ? xor_1_out : 1'bz;  // Controlled_Buffer controlled_buffer_1
  assign c1 = in_1 ? xor_2_out : 1'bz;  // Controlled_Buffer controlled_buffer_2
  assign c2 = in_1 ? xor_3_out : 1'bz;  // Controlled_Buffer controlled_buffer_3
  assign c3 = in_1 ? xor_4_out : 1'bz;  // Controlled_Buffer controlled_buffer_4
  assign c4 = in_1 ? xor_5_out : 1'bz;  // Controlled_Buffer controlled_buffer_5
  assign c5 = in_1 ? xor_6_out : 1'bz;  // Controlled_Buffer controlled_buffer_6
  assign c6 = in_1 ? xor_7_out : 1'bz;  // Controlled_Buffer controlled_buffer_7
  assign c7 = in_1 ? xor_8_out : 1'bz;  // Controlled_Buffer controlled_buffer_8
  xor xor_9 (c0_2, a0_2, b0_2);
  xor xor_10 (c1_2, a1_2, b1_2);
  xor xor_11 (c2_2, a2_2, b2_2);
  xor xor_12 (c3_2, a3_2, b3_2);
  xor xor_13 (c4_2, a4_2, b4_2);
  xor xor_14 (c5_2, a5_2, b5_2);
  xor xor_15 (c6_2, a6_2, b6_2);
  xor xor_16 (c7_2, a7_2, b7_2);

  // Notes on the sheet:
  //   8 Bit Xor Logic
endmodule
