// Logisim project barrelshifter.circ as structural Verilog: 2 circuits, main circuit main
module main (
  input  s0,
  input  s1,
  input  in_3,
  input  in_4,
  input  in_5,
  input  in_6,
  output out_7,
  output out_8,
  output out_9,
  output out_10
);

  _4to1_mux u_4to1_mux_1 (.s1(s1), .s0(s0), .x0(in_3), .x1(in_6), .x2(in_5), .x3(in_4), .y(out_7));
  _4to1_mux u_4to1_mux_2 (.s1(s1), .s0(s0), .x0(in_4), .x1(in_3), .x2(in_6), .x3(in_5), .y(out_8));
  _4to1_mux u_4to1_mux_3 (.s1(s1), .s0(s0), .x0(in_5), .x1(in_4), .x2(in_3), .x3(in_6), .y(out_9));
  _4to1_mux u_4to1_mux_4 (.s1(s1), .s0(s0), .x0(in_6), .x1(in_5), .x2(in_4), .x3(in_3), .y(out_10));
endmodule

module _4to1_mux (
  input  s1,
  input  s0,
  input  x0,
  input  x1,
  input  x2,
  input  x3,
  output y
);

  wire and_1_out, and_2_out, and_3_out, and_4_out, not_1_out, not_2_out;

  not not_1 (not_1_out, s1);
  not not_2 (not_2_out, s0);
  and and_1 (and_1_out, x0, not_1_out, not_2_out);
  and and_2 (and_2_out, x1, not_1_out, s0);
  and and_3 (and_3_out, x2, s1, not_2_out);
  and and_4 (and_4_out, x3, s1, s0);
  or or_1 (y, and_1_out, and_2_out, and_3_out, and_4_out);

  // Notes on the sheet:
  //   4 to 1 Multiplexer
endmodule
