// Logisim project carry.circ as structural Verilog: 2 circuits, main circuit main
module main (
  input  in_1,
  input  cin,
  input  a0,
  input  b0,
  input  a1,
  input  b1,
  input  a2,
  input  b2,
  input  a3,
  input  b3,
  input  a4,
  input  b4,
  input  a5,
  input  b5,
  input  a6,
  input  b6,
  input  a7,
  input  b7,
  input  a8,
  input  b8,
  input  a9,
  input  b9,
  input  a10,
  input  b10,
  input  a11,
  input  b11,
  input  a12,
  input  b12,
  input  a13,
  input  b13,
  input  a14,
  input  b14,
  input  a15,
  input  b15,
  output out_35,
  output out_36,
  output out_37,
  output out_38,
  output out_39,
  output out_40,
  output out_41,
  output out_42,
  output out_43,
  output out_44,
  output out_45,
  output out_46,
  output out_47,
  output out_48,
  output out_49,
  output out_50,
  output out_51
);

  wire n4_bit_cla_1_c4, n4_bit_cla_2_c4, n4_bit_cla_3_c4, n4_bit_cla_4_c3, n4_bit_cla_4_c4, xor_1_out,
       xor_2_out, xor_3_out, xor_4_out, xor_5_out, xor_6_out, xor_7_out, xor_8_out, xor_9_out, xor_10_out,
       xor_11_out, xor_12_out, xor_13_out, xor_14_out, xor_15_out, xor_16_out;

  xor xor_1 (xor_1_out, b0, in_1);
  xor xor_2 (xor_2_out, b1, in_1);
  xor xor_3 (xor_3_out, b2, in_1);
  xor xor_4 (xor_4_out, b3, in_1);
  xor xor_5 (xor_5_out, b4, in_1);
  xor xor_6 (xor_6_out, b5, in_1);
  xor xor_7 (xor_7_out, b6, in_1);
  xor xor_8 (xor_8_out, b7, in_1);
  xor xor_9 (xor_9_out, b8, in_1);
  xor xor_10 (xor_10_out, b9, in_1);
  xor xor_11 (xor_11_out, b10, in_1);
  xor xor_12 (xor_12_out, b11, in_1);
  xor xor_13 (xor_13_out, b12, in_1);
  xor xor_14 (xor_14_out, b13, in_1);
  xor xor_15 (xor_15_out, b14, in_1);
  xor xor_16 (xor_16_out, b15, in_1);
  _4_bit_cla u_4_bit_cla_1 (
    .cin(cin), .a0(a0), .b0(xor_1_out), .a1(a1), .b1(xor_2_out), .a2(a2), .b2(xor_3_out), .a3(a3),
    .b3(xor_4_out), .s0(out_35), .s1(out_36), .s2(out_37), .s3(out_38), .c4(n4_bit_cla_1_c4));  // open: c1, c2, c3
  _4_bit_cla u_4_bit_cla_2 (
    .cin(n4_bit_cla_1_c4), .a0(a4), .b0(xor_5_out), .a1(a5), .b1(xor_6_out), .a2(a6), .b2(xor_7_out),
    .a3(a7), .b3(xor_8_out), .s0(out_39), .s1(out_40), .s2(out_41), .s3(out_42), .c4(n4_bit_cla_2_c4));  // open: c1, c2, c3
  _4_bit_cla u_4_bit_cla_3 (
    .cin(n4_bit_cla_2_c4), .a0(a8), .b0(xor_9_out), .a1(a9), .b1(xor_10_out), .a2(a10), .b2(xor_11_out),
    .a3(a11), .b3(xor_12_out), .s0(out_43), .s1(out_44), .s2(out_45), .s3(out_46), .c4(n4_bit_cla_3_c4));  // open: c1, c2, c3
  _4_bit_cla u_4_bit_cla_4 (
    .cin(n4_bit_cla_3_c4), .a0(a12), .b0(xor_13_out), .a1(a13), .b1(xor_14_out), .a2(a14), .b2(xor_15_out),
    .a3(a15), .b3(xor_16_out), .s0(out_47), .s1(out_48), .s2(out_49), .c3(n4_bit_cla_4_c3), .s3(out_50),
    .c4(n4_bit_cla_4_c4));  // open: c1, c2
  xor xor_17 (out_51, n4_bit_cla_4_c3, n4_bit_cla_4_c4);
endmodule

module _4_bit_cla (
  input  cin,
  input  a0,
  input  b0,
  input  a1,
  input  b1,
  input  a2,
  input  b2,
  input  a3,
  input  b3,
  output s0,
  output c1,
  output s1,
  output c2,
  output s2,
  output c3,
  output s3,
  output c4
);

  wire and_1_out, and_2_out, and_3_out, and_4_out, and_5_out, and_6_out, and_7_out, and_8_out, and_9_out,
       and_10_out, g0_out, g1_out, g2_out, g3_out, p0_out, p1_out, p2_out, p3_out;

  xor p0 (p0_out, a0, b0);
  and g0 (g0_out, a0, b0);
  xor p1 (p1_out, a1, b1);
  and g1 (g1_out, a1, b1);
  xor p2 (p2_out, a2, b2);
  and g2 (g2_out, a2, b2);
  xor p3 (p3_out, a3, b3);
  and g3 (g3_out, a3, b3);
  and and_1 (and_1_out, g0_out, p1_out);
  and and_2 (and_2_out, g1_out, p2_out);
  and and_3 (and_3_out, g2_out, p3_out);
  and and_4 (and_4_out, p3_out, p2_out, p1_out, g0_out);
  and and_5 (and_5_out, cin, p0_out);
  and and_6 (and_6_out, g0_out, p2_out, p1_out);
  and and_7 (and_7_out, p3_out, p2_out, p1_out, p0_out, cin);
  and and_8 (and_8_out, cin, p1_out, p0_out);
  and and_9 (and_9_out, cin, p0_out, p2_out, p1_out);
  and and_10 (and_10_out, g1_out, p2_out, p3_out);
  or or_1 (c1, and_5_out, g0_out);
  or or_2 (c2, and_1_out, and_8_out, g1_out);
  or or_3 (c3, and_2_out, g2_out, and_6_out, and_9_out);
  or or_4 (c4, and_10_out, and_3_out, g3_out, and_4_out, and_7_out);
  xor xor_1 (s0, cin, p0_out);
  xor xor_2 (s1, c1, p1_out);
  xor xor_3 (s2, c2, p2_out);
  xor xor_4 (s3, c3, p3_out);
endmodule
