// Logisim project fulladder.circ as structural Verilog: 3 circuits, main circuit main
module main (
  input  in_1,
  input  in_2,
  input  in_3,
  input  in_4,
  input  in_5,
  input  in_6,
  input  in_7,
  input  in_8,
  input  in_9,
  output out_10,
  output out_11,
  output out_12,
  output out_13,
  output out_14
);

  wire full_adder_1_out_5, full_adder_2_out_5, full_adder_3_out_5;

  full_adder full_adder_1 (.in_1(in_2), .in_2(in_3), .in_3(in_1), .out_4(out_10), .out_5(full_adder_1_out_5));
  full_adder full_adder_2 (
    .in_1(in_4), .in_2(in_5), .in_3(full_adder_1_out_5), .out_4(out_11), .out_5(full_adder_2_out_5));
  full_adder full_adder_3 (
    .in_1(in_6), .in_2(in_7), .in_3(full_adder_2_out_5), .out_4(out_12), .out_5(full_adder_3_out_5));
  full_adder full_adder_4 (.in_1(in_8), .in_2(in_9), .in_3(full_adder_3_out_5), .out_4(out_13), .out_5(out_14));
endmodule

module full_adder (
  input  in_1,
  input  in_2,
  input  in_3,
  output out_4,
  output out_5
);

  wire and_1_out, and_2_out, xor_1_out;

  xor xor_1 (xor_1_out, in_1, in_2);
  and and_1 (and_1_out, in_1, in_2);
  xor xor_2 (out_4, xor_1_out, in_3);
  and and_2 (and_2_out, xor_1_out, in_3);
  or or_1 (out_5, and_1_out, and_2_out);
endmodule

module half_adder (
  input  in_1,
  input  in_2,
  output out_3,
  output out_4
);

  xor xor_1 (out_3, in_1, in_2);
  and and_1 (out_4, in_1, in_2);
endmodule
