// Logisim project q5.circ as structural Verilog: 2 circuits, main circuit main
module main (
  input  s0,
  input  s1,
  input  in_3,
  input  in_4,
  output out_5
);

  wire and_1_out, not_1_out, or_1_out, xor_1_out;

  and and_1 (and_1_out, in_3, in_4);
  or or_1 (or_1_out, in_3, in_4);
  not not_1 (not_1_out, in_3);
  xor xor_1 (xor_1_out, in_3, in_4);
  _4to1_mux u_4to1_mux_1 (.s1(s1), .s0(s0), .x0(and_1_out), .x1(or_1_out), .x2(not_1_out), .x3(xor_1_out), .y(out_5));
endmodule

module _4to1_mux (
  input  s1,
  input  s0,
  input  x0,
  input  x1,
  input  x2,
  input  x3,
  output y
);

  wire and_1_out, and_2_out, and_3_out, and_4_out, not_1_out, not_2_out;

  not not_1 (not_1_out, s1);
  not not_2 (not_2_out, s0);
  and and_1 (and_1_out, x0, not_1_out, not_2_out);
  and and_2 (and_2_out, x1, not_1_out, s0);
  and and_3 (and_3_out, x2, s1, not_2_out);
  and and_4 (and_4_out, x3, s1, s0);
  or or_1 (y, and_1_out, and_2_out, and_3_out, and_4_out);

  // Notes on the sheet:
  //   4 to 1 Multiplexer
endmodule
