// Logisim project q5final.circ as structural Verilog: 3 circuits, main circuit main
module main (
  input  s0,
  input  s1,
  input  in_3,
  input  in_4,
  input  in_5,
  input  in_6,
  input  in_7,
  input  in_8,
  input  in_9,
  input  in_10,
  input  in_11,
  input  in_12,
  input  in_13,
  input  in_14,
  input  in_15,
  input  in_16,
  input  in_17,
  input  in_18,
  input  in_19,
  input  in_20,
  input  in_21,
  input  in_22,
  input  in_23,
  input  in_24,
  input  in_25,
  input  in_26,
  input  in_27,
  input  in_28,
  input  in_29,
  input  in_30,
  input  in_31,
  input  in_32,
  input  in_33,
  input  in_34,
  input  in_35,
  input  in_36,
  input  in_37,
  input  in_38,
  input  in_39,
  input  in_40,
  input  in_41,
  input  in_42,
  input  in_43,
  input  in_44,
  input  in_45,
  input  in_46,
  input  in_47,
  input  in_48,
  input  in_49,
  input  in_50,
  input  in_51,
  input  in_52,
  input  in_53,
  input  in_54,
  input  in_55,
  input  in_56,
  input  in_57,
  input  in_58,
  input  in_59,
  input  in_60,
  input  in_61,
  input  in_62,
  input  in_63,
  input  in_64,
  input  in_65,
  input  in_66,
  output out_67,
  output out_68,
  output out_69,
  output out_70,
  output out_71,
  output out_72,
  output out_73,
  output out_74,
  output out_75,
  output out_76,
  output out_77,
  output out_78,
  output out_79,
  output out_80,
  output out_81,
  output out_82,
  output out_83,
  output out_84,
  output out_85,
  output out_86,
  output out_87,
  output out_88,
  output out_89,
  output out_90,
  output out_91,
  output out_92,
  output out_93,
  output out_94,
  output out_95,
  output out_96,
  output out_97,
  output out_98
);

  oneunit oneunit_1 (.in_3(in_3), .in_4(in_6), .s0(s0), .s1(s1), .out_5(out_67));
  oneunit oneunit_2 (.in_3(in_9), .in_4(in_12), .s0(s0), .s1(s1), .out_5(out_70));
  oneunit oneunit_3 (.in_3(in_15), .in_4(in_18), .s0(s0), .s1(s1), .out_5(out_73));
  oneunit oneunit_4 (.in_3(in_21), .in_4(in_24), .s0(s0), .s1(s1), .out_5(out_76));
  oneunit oneunit_5 (.in_3(in_27), .in_4(in_30), .s0(s0), .s1(s1), .out_5(out_79));
  oneunit oneunit_6 (.in_3(in_33), .in_4(in_36), .s0(s0), .s1(s1), .out_5(out_82));
  oneunit oneunit_7 (.in_3(in_39), .in_4(in_42), .s0(s0), .s1(s1), .out_5(out_85));
  oneunit oneunit_8 (.in_3(in_45), .in_4(in_48), .s0(s0), .s1(s1), .out_5(out_88));
  oneunit oneunit_9 (.in_3(in_51), .in_4(in_53), .s0(s0), .s1(s1), .out_5(out_91));
  oneunit oneunit_10 (.in_3(in_55), .in_4(in_57), .s0(s0), .s1(s1), .out_5(out_93));
  oneunit oneunit_11 (.in_3(in_59), .in_4(in_61), .s0(s0), .s1(s1), .out_5(out_95));
  oneunit oneunit_12 (.in_3(in_63), .in_4(in_65), .s0(s0), .s1(s1), .out_5(out_97));
  oneunit oneunit_13 (.in_3(in_4), .in_4(in_7), .s0(s0), .s1(s1), .out_5(out_68));
  oneunit oneunit_14 (.in_3(in_10), .in_4(in_13), .s0(s0), .s1(s1), .out_5(out_71));
  oneunit oneunit_15 (.in_3(in_16), .in_4(in_19), .s0(s0), .s1(s1), .out_5(out_74));
  oneunit oneunit_16 (.in_3(in_22), .in_4(in_25), .s0(s0), .s1(s1), .out_5(out_77));
  oneunit oneunit_17 (.in_3(in_28), .in_4(in_31), .s0(s0), .s1(s1), .out_5(out_80));
  oneunit oneunit_18 (.in_3(in_34), .in_4(in_37), .s0(s0), .s1(s1), .out_5(out_83));
  oneunit oneunit_19 (.in_3(in_40), .in_4(in_43), .s0(s0), .s1(s1), .out_5(out_86));
  oneunit oneunit_20 (.in_3(in_46), .in_4(in_49), .s0(s0), .s1(s1), .out_5(out_89));
  oneunit oneunit_21 (.in_3(in_52), .in_4(in_54), .s0(s0), .s1(s1), .out_5(out_92));
  oneunit oneunit_22 (.in_3(in_56), .in_4(in_58), .s0(s0), .s1(s1), .out_5(out_94));
  oneunit oneunit_23 (.in_3(in_60), .in_4(in_62), .s0(s0), .s1(s1), .out_5(out_96));
  oneunit oneunit_24 (.in_3(in_64), .in_4(in_66), .s0(s0), .s1(s1), .out_5(out_98));
  oneunit oneunit_25 (.in_3(in_5), .in_4(in_8), .s0(s0), .s1(s1), .out_5(out_69));
  oneunit oneunit_26 (.in_3(in_11), .in_4(in_14), .s0(s0), .s1(s1), .out_5(out_72));
  oneunit oneunit_27 (.in_3(in_17), .in_4(in_20), .s0(s0), .s1(s1), .out_5(out_75));
  oneunit oneunit_28 (.in_3(in_23), .in_4(in_26), .s0(s0), .s1(s1), .out_5(out_78));
  oneunit oneunit_29 (.in_3(in_29), .in_4(in_32), .s0(s0), .s1(s1), .out_5(out_81));
  oneunit oneunit_30 (.in_3(in_35), .in_4(in_38), .s0(s0), .s1(s1), .out_5(out_84));
  oneunit oneunit_31 (.in_3(in_41), .in_4(in_44), .s0(s0), .s1(s1), .out_5(out_87));
  oneunit oneunit_32 (.in_3(in_47), .in_4(in_50), .s0(s0), .s1(s1), .out_5(out_90));
endmodule

module oneunit (
  input  s0,
  input  s1,
  input  in_3,
  input  in_4,
  output out_5
);

  wire and_1_out, not_1_out, or_1_out, xor_1_out;

  and and_1 (and_1_out, in_3, in_4);
  or or_1 (or_1_out, in_3, in_4);
  not not_1 (not_1_out, in_3);
  xor xor_1 (xor_1_out, in_3, in_4);
  _4to1_mux u_4to1_mux_1 (.s1(s1), .s0(s0), .x0(and_1_out), .x1(or_1_out), .x2(not_1_out), .x3(xor_1_out), .y(out_5));
endmodule

module _4to1_mux (
  input  s1,
  input  s0,
  input  x0,
  input  x1,
  input  x2,
  input  x3,
  output y
);

  wire and_1_out, and_2_out, and_3_out, and_4_out, not_1_out, not_2_out;

  not not_1 (not_1_out, s1);
  not not_2 (not_2_out, s0);
  and and_1 (and_1_out, x0, not_1_out, not_2_out);
  and and_2 (and_2_out, x1, not_1_out, s0);
  and and_3 (and_3_out, x2, s1, not_2_out);
  and and_4 (and_4_out, x3, s1, s0);
  or or_1 (y, and_1_out, and_2_out, and_3_out, and_4_out);

  // Notes on the sheet:
  //   4 to 1 Multiplexer
endmodule
